# Fritzing sketch Stepper Motor Schematic (saved by Fritzing 0.9.3b)
breadboards: 1

parts:
  Part1 = Arduino Uno (Rev3)
  C1 = Electrolytic Capacitor [capacitance=100µF voltage=50V package="100 mil [THT, electrolytic]"]
  M1 = Stepper Motor - Bipolar
  Power_plug1 = Power plug
  Part2 = Arduino Nano (Rev3.0)
  Pololu_A1 = Pololu A4988 [package=SO16]
  Pololu_A2 = Pololu A4988 [package=SO16]
  C2 = Electrolytic Capacitor [capacitance=1µF package="100 mil [THT, electrolytic]"]
  M2 = Stepper Motor - Bipolar

nets:
  N1: Part1.D8, Pololu_A1.MS1
  N2: Part1.D9_PWM, Pololu_A1.ENABLE
  N3: Part1.D2, Pololu_A1.DIR
  N4: Part1.D3_PWM, Pololu_A1.STEP
  N5: Part1.D4, Pololu_A1.SLEEP
  N6: Part1.D5_PWM, Pololu_A1.RESET
  N7: Part1.D6_PWM, Pololu_A1.MS3
  N8: Part1.D7, Pololu_A1.MS2
  VDD: Part1.5V, Pololu_A1.VDD, Pololu_A2.VDD
  N9: Part1.GND, Pololu_A1.GND#8, Pololu_A2.GND#8
  N10: C1.-, Power_plug1.GND, Pololu_A1.GND#14, Pololu_A2.GND#14, C2.-
  N11: C1.+, Power_plug1.VCC, Pololu_A1.VMOT, Pololu_A2.VMOT, C2.+
  N12: M1.A, Pololu_A1.1B
  N13: M1.C, Pololu_A1.1A
  N14: M1.B, Pololu_A1.2A
  N15: M1.D, Pololu_A1.2B
  N16: Part2.D2, Pololu_A2.DIR
  N17: Part2.D3, Pololu_A2.STEP
  N18: Part2.D4, Pololu_A2.SLEEP
  N19: Part2.D5, Pololu_A2.RESET
  N20: Part2.D6, Pololu_A2.MS3
  N21: Part2.D7, Pololu_A2.MS2
  N22: Part2.D8, Pololu_A2.MS1
  N23: Part2.D9, Pololu_A2.ENABLE
  N24: Pololu_A2.1B, M2.A
  N25: Pololu_A2.1A, M2.C
  N26: Pololu_A2.2A, M2.B
  N27: Pololu_A2.2B, M2.D
